// Logisim project CRCs-code.circ as structural Verilog: 2 circuits, main circuit main
module main (
  input  [7:0] data,
  input  [3:0] \除数 ,
  output [10:0] \output 
);

  wire [10:0] bit_extender_1_out, data_t;

  BitSelector #(.width(11), .group(4)) bitselector_1 (.in(data_t));  // open: out, sel
  assign bit_extender_1_out = {{3{1'b0}}, data};  // Bit_Extender bit_extender_1
  Shifter #(.width(11)) shifter_1 (.in(bit_extender_1_out), .\dist (4'b0011), .out(data_t));
  division division_1 ();  // open: 被除数, 除数, _3位余数, 商
endmodule

module division (
  input  [3:0] \被除数 ,
  input  [3:0] \除数 ,
  output [2:0] \_3位余数 ,
  output \商 
);

  wire [3:0] xor_1_out;
  wire [3:3] multiplexer_1_out;

  BitSelector #(.width(4)) bitselector_1 (.in(\被除数 ), .out(\商 ), .sel(2'b11));
  assign xor_1_out = \被除数  ^ \除数 ;  // XOR_Gate xor_1, 4 bits wide
  Multiplexer #(.width(4)) multiplexer_1 (
    .in0(\被除数 ), .in1(xor_1_out), .out({multiplexer_1_out[3], \_3位余数 }), .sel(\商 ));  // open: en

  // Other names for the same wires on the sheet: num[3:0] = \被除数 ; quotient = \商 

  // Notes on the sheet:
  //   首位必为1
  //   四位模二除法器
  //   等价于异或运算
endmodule
