// Logisim project pre_sokoban.circ as structural Verilog: 2 circuits, main circuit main
module main (
  input  dx,
  input  dy,
  input  reset,
  output \output 
);

  wire not_1_out;
  wire [2:0] x;

  Clock clock_1 ();  // open: out
  Adder #(.width(3)) adder_1 (.b(x));  // open: a, out, cin, cout
  not not_1 (not_1_out, reset);
  buf and_1 (\output , not_1_out);  // AND_Gate
endmodule

module is_valid (
  input  [2:0] x,
  input  [2:0] y,
  output out_3
);

  wire and_2_out, comparator_1_eq, comparator_2_eq, comparator_3_eq, comparator_4_eq, comparator_5_eq,
       comparator_6_eq, comparator_7_eq, comparator_8_eq, comparator_9_eq, comparator_10_eq,
       comparator_11_eq, comparator_12_eq, comparator_13_lt, comparator_14_lt, nand_1_out, nand_2_out,
       nand_3_out, nand_4_out, nand_5_out, nand_6_out;

  Comparator #(.width(3)) comparator_1 (.a(x), .b(3'b001), .eq(comparator_1_eq));  // open: gt, lt
  Comparator #(.width(3)) comparator_2 (.a(y), .b(3'b001), .eq(comparator_2_eq));  // open: gt, lt
  nand nand_1 (nand_1_out, comparator_2_eq, comparator_1_eq);
  Comparator #(.width(3)) comparator_3 (.a(x), .b(3'b001), .eq(comparator_3_eq));  // open: gt, lt
  Comparator #(.width(3)) comparator_4 (.a(y), .b(3'b010), .eq(comparator_4_eq));  // open: gt, lt
  nand nand_2 (nand_2_out, comparator_4_eq, comparator_3_eq);
  Comparator #(.width(3)) comparator_5 (.a(x), .b(3'b010), .eq(comparator_5_eq));  // open: gt, lt
  Comparator #(.width(3)) comparator_6 (.a(y), .b(3'b001), .eq(comparator_6_eq));  // open: gt, lt
  nand nand_3 (nand_3_out, comparator_6_eq, comparator_5_eq);
  Comparator #(.width(3)) comparator_7 (.a(x), .b(3'b011), .eq(comparator_7_eq));  // open: gt, lt
  Comparator #(.width(3)) comparator_8 (.a(y), .b(3'b100), .eq(comparator_8_eq));  // open: gt, lt
  nand nand_4 (nand_4_out, comparator_8_eq, comparator_7_eq);
  and and_1 (out_3, nand_1_out, nand_2_out, nand_3_out, nand_4_out, nand_5_out, nand_6_out, and_2_out);
  Comparator #(.width(3)) comparator_9 (.a(x), .b(3'b100), .eq(comparator_9_eq));  // open: gt, lt
  Comparator #(.width(3)) comparator_10 (.a(y), .b(3'b011), .eq(comparator_10_eq));  // open: gt, lt
  nand nand_5 (nand_5_out, comparator_10_eq, comparator_9_eq);
  Comparator #(.width(3)) comparator_11 (.a(x), .b(3'b100), .eq(comparator_11_eq));  // open: gt, lt
  Comparator #(.width(3)) comparator_12 (.a(y), .b(3'b100), .eq(comparator_12_eq));  // open: gt, lt
  nand nand_6 (nand_6_out, comparator_12_eq, comparator_11_eq);
  Comparator #(.width(3), .mode("unsigned")) comparator_13 (.a(x), .b(3'b110), .lt(comparator_13_lt));  // open: gt, eq
  Comparator #(.width(3), .mode("unsigned")) comparator_14 (.a(y), .b(3'b110), .lt(comparator_14_lt));  // open: gt, eq
  and and_2 (and_2_out, comparator_14_lt, comparator_13_lt);
endmodule
